// Logisim project CPU.circ as structural Verilog: 7 circuits, main circuit main
module main (
  input  [15:0] in_1,
  input  [15:0] in_2,
  input  [15:0] in_3,
  input  W_E,
  input  Clear,
  input  [15:0] in_6,
  input  W_E_2,
  input  [15:0] in_8,
  input  [15:0] in_9,
  input  [3:0] in_10,
  input  [15:0] in_11,
  input  [15:0] in_12,
  input  [3:0] in_13,
  output [15:0] out_14,
  output [15:0] out_15,
  output [15:0] Read_Data_1,
  output [15:0] out_17,
  output [15:0] Read_Data_2,
  output [15:0] out_19
);

  wire and_1_out, and_2_out, clock_1_out, comparator_1_lt, comparator_2_eq, comparator_2_gt, comparator_2_lt,
       comparator_3_eq, decode_1_branch, decode_1_i_type, decode_1_load, decode_1_store,
       decode_1_writes_to_reg, or_1_out;
  wire [3:0] decode_1_dest, decode_1_opcode, decode_1_sr1, decode_1_sr2, multiplexer_3_out,
       register_file_1_read_data_1, register_file_1_read_data_1_2, register_file_1_read_data_1_3,
       register_file_1_read_data_1_4;
  wire [5:0] A_out;
  wire [14:0] bit_extender_3_out;
  wire [15:0] bit_extender_2_out, decode_1_immediate, fetch_1_out_8, multiplexer_1_out, multiplexer_2_out,
       multiplexer_4_out, register_file_1_read_data_2, screen_memory_1_output_1, screen_memory_1_output_2,
       screen_memory_1_output_2_2, screen_memory_1_output_4, screen_memory_1_output_5,
       screen_memory_1_output_6, screen_memory_1_output_7, screen_memory_1_output_8,
       screen_memory_1_output_9, screen_memory_1_output_10, screen_memory_1_output_11,
       screen_memory_1_output_12, screen_memory_1_output_13, screen_memory_1_output_14,
       screen_memory_1_output_15, screen_memory_1_output_16;

  Button button (.out(A_out[3]));
  Button button_2 (.out(A_out[4]));
  Button button_3 (.out(A_out[5]));
  Button button_4 (.out(A_out[2]));
  Bit_Extender #(.in_width(16), .out_width(4)) bit_extender_1 ();  // open: in, out
  Comparator #(.width(16), .mode("unsigned")) comparator_1 (
    .a({register_file_1_read_data_1_4, register_file_1_read_data_1_3, register_file_1_read_data_1_2, register_file_1_read_data_1}),
    .b(16'h8010), .lt(comparator_1_lt));  // open: gt, eq
  Comparator #(.width(16), .mode("unsigned")) comparator_2 (
    .a({register_file_1_read_data_1_4, register_file_1_read_data_1_3, register_file_1_read_data_1_2, register_file_1_read_data_1}),
    .b(16'h8000), .gt(comparator_2_gt), .eq(comparator_2_eq), .lt(comparator_2_lt));
  Button B (.out(A_out[1]));
  Button A (.out(A_out[0]));
  Screen_Memory screen_memory_1 (
    .Write_Data(register_file_1_read_data_2), .W_E(and_2_out), .Write_Address(register_file_1_read_data_1),
    .Clock(clock_1_out), .Clear(Clear), .Output_1(screen_memory_1_output_1),
    .Output_2(screen_memory_1_output_2), .Output_2_2(screen_memory_1_output_2_2),
    .Output_4(screen_memory_1_output_4), .Output_5(screen_memory_1_output_5),
    .Output_6(screen_memory_1_output_6), .Output_7(screen_memory_1_output_7),
    .Output_8(screen_memory_1_output_8), .Output_9(screen_memory_1_output_9),
    .Output_10(screen_memory_1_output_10), .Output_11(screen_memory_1_output_11),
    .Output_12(screen_memory_1_output_12), .Output_13(screen_memory_1_output_13),
    .Output_14(screen_memory_1_output_14), .Output_15(screen_memory_1_output_15),
    .Output_16(screen_memory_1_output_16));
  assign bit_extender_2_out = {{10{1'b0}}, A_out};  // Bit_Extender bit_extender_2
  and and_1 (and_1_out, comparator_2_lt, decode_1_store);
  or or_1 (or_1_out, comparator_2_gt, comparator_2_eq);
  Multiplexer #(.width(16), .enable("false")) multiplexer_1 (
    .in0(out_15), .in1(bit_extender_2_out), .out(multiplexer_1_out), .sel(comparator_3_eq));
  Comparator #(.width(16), .mode("unsigned")) comparator_3 (
    .a({register_file_1_read_data_1_4, register_file_1_read_data_1_3, register_file_1_read_data_1_2, register_file_1_read_data_1}),
    .b(16'h8010), .eq(comparator_3_eq));  // open: gt, lt
  DotMatrix #(.inputtype("row"), .matrixcols(16), .matrixrows(16)) dotmatrix_1 (
    .row0(screen_memory_1_output_1), .row1(screen_memory_1_output_2), .row2(screen_memory_1_output_2_2),
    .row3(screen_memory_1_output_4), .row4(screen_memory_1_output_5), .row5(screen_memory_1_output_6),
    .row6(screen_memory_1_output_7), .row7(screen_memory_1_output_8), .row8(screen_memory_1_output_9),
    .row9(screen_memory_1_output_10), .row10(screen_memory_1_output_11), .row11(screen_memory_1_output_12),
    .row12(screen_memory_1_output_13), .row13(screen_memory_1_output_14), .row14(screen_memory_1_output_15),
    .row15(screen_memory_1_output_16));
  Bit_Extender #(.in_width(16), .out_width(15)) bit_extender_3 (
    .in({register_file_1_read_data_1_4, register_file_1_read_data_1_3, register_file_1_read_data_1_2, register_file_1_read_data_1}),
    .out(bit_extender_3_out));
  and and_2 (and_2_out, or_1_out, decode_1_store, comparator_1_lt);
  RAM #(.addrWidth(15), .dataWidth(16), .bus("separate")) ram_1 (
    .addr(bit_extender_3_out), .din(register_file_1_read_data_2), .data(out_15), .str(and_1_out),
    .clk(clock_1_out), .clr(Clear));  // open: sel, ld
  // Probe on decode_1_opcode
  Multiplexer #(.width(16)) multiplexer_2 (
    .in0(out_14), .in1(multiplexer_1_out), .out(multiplexer_2_out), .sel(decode_1_load));  // open: en
  Fetch fetch_1 (
    .Immediate(decode_1_immediate), .ALU_Output(out_14), .Is_Branch(decode_1_branch), .Clock(clock_1_out),
    .Clear(Clear), .out_8(fetch_1_out_8));  // open: Is_branch_taken_comes_from_alu, Is_branch_comes_from_decode
  // Probe on fetch_1_out_8
  ALU alu_1 (.Input_1(in_11), .Input_2(in_12), .Opcode(in_13), .Output(out_19));
  Decode decode_1 (
    .Fetch(fetch_1_out_8), .Sr1(decode_1_sr1), .Opcode(decode_1_opcode), .Sr2(decode_1_sr2),
    .Dest(decode_1_dest), .Immediate(decode_1_immediate), .Load(decode_1_load), .Store(decode_1_store),
    .Branch(decode_1_branch), .Writes_to_reg(decode_1_writes_to_reg), .I_Type(decode_1_i_type));
  ALU alu_2 (.Input_1(in_8), .Input_2(in_9), .Opcode(in_10), .Output(out_17));
  Clock clock_1 (.out(clock_1_out));
  Register_File register_file_1 (
    .Write_Data(multiplexer_2_out), .W_E(decode_1_writes_to_reg), .Write_Address(decode_1_dest),
    .Clock(clock_1_out), .Clear(Clear), .Read_Address_1(multiplexer_3_out), .Read_Address_2(decode_1_sr2),
    .Read_Data_1({register_file_1_read_data_1_4, register_file_1_read_data_1_3, register_file_1_read_data_1_2, register_file_1_read_data_1}),
    .Read_Data_2(register_file_1_read_data_2));
  Multiplexer #(.width(4)) multiplexer_3 (
    .in0(decode_1_sr1), .in1(decode_1_dest), .out(multiplexer_3_out), .sel(decode_1_i_type));  // open: en
  Multiplexer #(.width(16)) multiplexer_4 (
    .in0(register_file_1_read_data_2), .in1(decode_1_immediate), .out(multiplexer_4_out),
    .sel(decode_1_i_type));  // open: en
  ALU alu_3 (
    .Input_1({register_file_1_read_data_1_4, register_file_1_read_data_1_3, register_file_1_read_data_1_2, register_file_1_read_data_1}),
    .Input_2(multiplexer_4_out), .Opcode(decode_1_opcode), .Output(out_14));
  // Probe on out_14

  // Other names for the same wires on the sheet: ALUO[15:0] = out_14

  // Notes on the sheet:
  //   Execute
  //   sr1
  //   sr2
endmodule

module ALU (
  input  [15:0] Input_1,
  input  [15:0] Input_2,
  input  [3:0] Opcode,
  output [15:0] Output
);

  wire comparator_1_lt, comparator_2_eq, comparator_3_eq, not_1_out;
  wire [3:0] bit_extender_3_out, bit_extender_4_out;
  wire [15:0] _0_out, _1_out, _2_out, _3_out, adder_1_out, bit_extender_1_out, bit_extender_2_out,
       bit_extender_5_out, bit_extender_6_out, bit_extender_7_out, bit_extender_8_out, multiplier_1_out,
       shifter_1_out, shifter_2_out, subtractor_1_out;

  assign bit_extender_1_out = {{15{1'b0}}, 1'b0};  // Bit_Extender bit_extender_1
  assign bit_extender_2_out = {{15{1'b0}}, 1'b0};  // Bit_Extender bit_extender_2
  Bit_Extender #(.in_width(16), .out_width(4)) bit_extender_3 (.in(Input_2), .out(bit_extender_3_out));
  Bit_Extender #(.in_width(16), .out_width(4)) bit_extender_4 (.in(Input_2), .out(bit_extender_4_out));
  assign _0_out = Input_1 & Input_2;  // AND_Gate _0, 16 bits wide
  assign _1_out = Input_1 | Input_2;  // OR_Gate _1, 16 bits wide
  assign _2_out = Input_1 ^ Input_2;  // XOR_Gate _2, 16 bits wide
  assign _3_out = ~Input_1;  // NOT_Gate _3, 16 bits wide
  Adder #(.width(16)) adder_1 (.a(Input_1), .b(Input_2), .out(adder_1_out));  // open: cin, cout
  Subtractor #(.width(16)) subtractor_1 (.a(Input_1), .b(Input_2), .out(subtractor_1_out));  // open: bin, bout
  Multiplier #(.width(16)) multiplier_1 (.a(Input_1), .b(Input_2), .out(multiplier_1_out));  // open: cin, cout
  Comparator #(.width(16)) comparator_1 (.a(Input_1), .b(Input_2), .lt(comparator_1_lt));  // open: gt, eq
  Shifter #(.width(16)) shifter_1 (.in(Input_1), .\dist (bit_extender_3_out), .out(shifter_1_out));
  Shifter #(.width(16), .shift("ar")) shifter_2 (.in(Input_1), .\dist (bit_extender_4_out), .out(shifter_2_out));
  assign bit_extender_5_out = {{15{1'b0}}, 1'b1};  // Bit_Extender bit_extender_5
  Comparator #(.width(16)) comparator_2 (.a(Input_1), .b(bit_extender_1_out), .eq(comparator_2_eq));  // open: gt, lt
  not not_1 (not_1_out, comparator_3_eq);
  Comparator #(.width(16), .mode("unsigned")) comparator_3 (
    .a(Input_1), .b(bit_extender_2_out), .eq(comparator_3_eq));  // open: gt, lt
  assign bit_extender_6_out = {{15{1'b0}}, comparator_1_lt};  // Bit_Extender bit_extender_6
  assign bit_extender_7_out = {{15{1'b0}}, comparator_2_eq};  // Bit_Extender bit_extender_7
  assign bit_extender_8_out = {{15{1'b0}}, not_1_out};  // Bit_Extender bit_extender_8
  Multiplexer #(.select(4), .width(16)) multiplexer_1 (
    .in0(_0_out), .in1(_1_out), .in2(_2_out), .in3(_3_out), .in4(adder_1_out), .in5(subtractor_1_out),
    .in6(multiplier_1_out), .in7(bit_extender_6_out), .in8(shifter_1_out), .in9(shifter_2_out),
    .in10(Input_1), .in11(Input_1), .in12(Input_2), .in13(bit_extender_5_out), .in14(bit_extender_7_out),
    .in15(bit_extender_8_out), .out(Output), .sel(Opcode));  // open: en
endmodule

// Register
module Register_File (
  input  [15:0] Write_Data,
  input  [3:0] Read_Address_1,
  input  [3:0] Read_Address_2,
  input  W_E,
  input  [3:0] Write_Address,
  input  Clock,
  input  Clear,
  output [15:0] Read_Data_1,
  output [15:0] Read_Data_2
);

  wire decoder_1_out0, decoder_1_out1, decoder_1_out2, decoder_1_out3, decoder_1_out4, decoder_1_out5,
       decoder_1_out6, decoder_1_out7, decoder_1_out8, decoder_1_out9, decoder_1_out10, decoder_1_out11,
       decoder_1_out12, decoder_1_out13, decoder_1_out14, decoder_1_out15;
  wire [15:0] register_1_q, register_2_q, register_3_q, register_4_q, register_5_q, register_6_q,
       register_7_q, register_8_q, register_9_q, register_10_q, register_11_q, register_12_q, register_13_q,
       register_14_q, register_15_q, register_16_q;

  Decoder #(.select(4), .disabled(0)) decoder_1 (
    .out0(decoder_1_out0), .out1(decoder_1_out1), .out2(decoder_1_out2), .out3(decoder_1_out3),
    .out4(decoder_1_out4), .out5(decoder_1_out5), .out6(decoder_1_out6), .out7(decoder_1_out7),
    .out8(decoder_1_out8), .out9(decoder_1_out9), .out10(decoder_1_out10), .out11(decoder_1_out11),
    .out12(decoder_1_out12), .out13(decoder_1_out13), .out14(decoder_1_out14), .out15(decoder_1_out15),
    .sel(Write_Address), .en(W_E));
  Register #(.width(16)) register_1 (.D(Write_Data), .en(decoder_1_out0), .Q(register_1_q), .clk(Clock), .clr(Clear));
  Register #(.width(16)) register_2 (.D(Write_Data), .en(decoder_1_out1), .Q(register_2_q), .clk(Clock), .clr(Clear));
  Register #(.width(16)) register_3 (.D(Write_Data), .en(decoder_1_out2), .Q(register_3_q), .clk(Clock), .clr(Clear));
  Register #(.width(16)) register_4 (.D(Write_Data), .en(decoder_1_out3), .Q(register_4_q), .clk(Clock), .clr(Clear));
  Register #(.width(16)) register_5 (.D(Write_Data), .en(decoder_1_out4), .Q(register_5_q), .clk(Clock), .clr(Clear));
  Register #(.width(16)) register_6 (.D(Write_Data), .en(decoder_1_out5), .Q(register_6_q), .clk(Clock), .clr(Clear));
  Register #(.width(16)) register_7 (.D(Write_Data), .en(decoder_1_out6), .Q(register_7_q), .clk(Clock), .clr(Clear));
  Register #(.width(16)) register_8 (.D(Write_Data), .en(decoder_1_out7), .Q(register_8_q), .clk(Clock), .clr(Clear));
  Register #(.width(16)) register_9 (.D(Write_Data), .en(decoder_1_out8), .Q(register_9_q), .clk(Clock), .clr(Clear));
  Register #(.width(16)) register_10 (.D(Write_Data), .en(decoder_1_out9), .Q(register_10_q), .clk(Clock), .clr(Clear));
  Register #(.width(16)) register_11 (
    .D(Write_Data), .en(decoder_1_out10), .Q(register_11_q), .clk(Clock), .clr(Clear));
  Register #(.width(16)) register_12 (
    .D(Write_Data), .en(decoder_1_out11), .Q(register_12_q), .clk(Clock), .clr(Clear));
  Register #(.width(16)) register_13 (
    .D(Write_Data), .en(decoder_1_out12), .Q(register_13_q), .clk(Clock), .clr(Clear));
  Register #(.width(16)) register_14 (
    .D(Write_Data), .en(decoder_1_out13), .Q(register_14_q), .clk(Clock), .clr(Clear));
  Register #(.width(16)) register_15 (
    .D(Write_Data), .en(decoder_1_out14), .Q(register_15_q), .clk(Clock), .clr(Clear));
  Register #(.width(16)) register_16 (
    .D(Write_Data), .en(decoder_1_out15), .Q(register_16_q), .clk(Clock), .clr(Clear));
  Multiplexer #(.select(4), .width(16)) multiplexer_1 (
    .in0(register_1_q), .in1(register_2_q), .in2(register_3_q), .in3(register_4_q), .in4(register_5_q),
    .in5(register_6_q), .in6(register_7_q), .in7(register_8_q), .in8(register_9_q), .in9(register_10_q),
    .in10(register_11_q), .in11(register_12_q), .in12(register_13_q), .in13(register_14_q),
    .in14(register_15_q), .in15(register_16_q), .out(Read_Data_1), .sel(Read_Address_1));  // open: en
  Multiplexer #(.select(4), .width(16)) multiplexer_2 (
    .in0(register_1_q), .in1(register_2_q), .in2(register_3_q), .in3(register_4_q), .in4(register_5_q),
    .in5(register_6_q), .in6(register_7_q), .in7(register_8_q), .in8(register_9_q), .in9(register_10_q),
    .in10(register_11_q), .in11(register_12_q), .in12(register_13_q), .in13(register_14_q),
    .in14(register_15_q), .in15(register_16_q), .out(Read_Data_2), .sel(Read_Address_2));  // open: en
endmodule

module Screen_Memory (
  input  [15:0] Write_Data,
  input  W_E,
  input  [3:0] Write_Address,
  input  Clock,
  input  Clear,
  output [15:0] Output_1,
  output [15:0] Output_2,
  output [15:0] Output_2_2,
  output [15:0] Output_4,
  output [15:0] Output_5,
  output [15:0] Output_6,
  output [15:0] Output_7,
  output [15:0] Output_8,
  output [15:0] Output_9,
  output [15:0] Output_10,
  output [15:0] Output_11,
  output [15:0] Output_12,
  output [15:0] Output_13,
  output [15:0] Output_14,
  output [15:0] Output_15,
  output [15:0] Output_16
);

  wire decoder_1_out0, decoder_1_out1, decoder_1_out2, decoder_1_out3, decoder_1_out4, decoder_1_out5,
       decoder_1_out6, decoder_1_out7, decoder_1_out8, decoder_1_out9, decoder_1_out10, decoder_1_out11,
       decoder_1_out12, decoder_1_out13, decoder_1_out14, decoder_1_out15;

  Decoder #(.select(4), .disabled(0)) decoder_1 (
    .out0(decoder_1_out0), .out1(decoder_1_out1), .out2(decoder_1_out2), .out3(decoder_1_out3),
    .out4(decoder_1_out4), .out5(decoder_1_out5), .out6(decoder_1_out6), .out7(decoder_1_out7),
    .out8(decoder_1_out8), .out9(decoder_1_out9), .out10(decoder_1_out10), .out11(decoder_1_out11),
    .out12(decoder_1_out12), .out13(decoder_1_out13), .out14(decoder_1_out14), .out15(decoder_1_out15),
    .sel(Write_Address), .en(W_E));
  Register #(.width(16)) register_1 (.D(Write_Data), .en(decoder_1_out0), .Q(Output_1), .clk(Clock), .clr(Clear));
  Register #(.width(16)) register_2 (.D(Write_Data), .en(decoder_1_out1), .Q(Output_2), .clk(Clock), .clr(Clear));
  Register #(.width(16)) register_3 (.D(Write_Data), .en(decoder_1_out2), .Q(Output_2_2), .clk(Clock), .clr(Clear));
  Register #(.width(16)) register_4 (.D(Write_Data), .en(decoder_1_out3), .Q(Output_4), .clk(Clock), .clr(Clear));
  Register #(.width(16)) register_5 (.D(Write_Data), .en(decoder_1_out4), .Q(Output_5), .clk(Clock), .clr(Clear));
  Register #(.width(16)) register_6 (.D(Write_Data), .en(decoder_1_out5), .Q(Output_6), .clk(Clock), .clr(Clear));
  Register #(.width(16)) register_7 (.D(Write_Data), .en(decoder_1_out6), .Q(Output_7), .clk(Clock), .clr(Clear));
  Register #(.width(16)) register_8 (.D(Write_Data), .en(decoder_1_out7), .Q(Output_8), .clk(Clock), .clr(Clear));
  Register #(.width(16)) register_9 (.D(Write_Data), .en(decoder_1_out8), .Q(Output_9), .clk(Clock), .clr(Clear));
  Register #(.width(16)) register_10 (.D(Write_Data), .en(decoder_1_out9), .Q(Output_10), .clk(Clock), .clr(Clear));
  Register #(.width(16)) register_11 (.D(Write_Data), .en(decoder_1_out10), .Q(Output_11), .clk(Clock), .clr(Clear));
  Register #(.width(16)) register_12 (.D(Write_Data), .en(decoder_1_out11), .Q(Output_12), .clk(Clock), .clr(Clear));
  Register #(.width(16)) register_13 (.D(Write_Data), .en(decoder_1_out12), .Q(Output_13), .clk(Clock), .clr(Clear));
  Register #(.width(16)) register_14 (.D(Write_Data), .en(decoder_1_out13), .Q(Output_14), .clk(Clock), .clr(Clear));
  Register #(.width(16)) register_15 (.D(Write_Data), .en(decoder_1_out14), .Q(Output_15), .clk(Clock), .clr(Clear));
  Register #(.width(16)) register_16 (.D(Write_Data), .en(decoder_1_out15), .Q(Output_16), .clk(Clock), .clr(Clear));
endmodule

module Fetch (
  input  Clock,
  input  Clear,
  input  [7:0] Is_branch_taken_comes_from_alu,
  input  [7:0] Is_branch_comes_from_decode,
  input  [15:0] Immediate,
  input  [15:0] ALU_Output,
  input  Is_Branch,
  output [15:0] out_8
);

  wire and_1_out, comparator_1_eq;
  wire [15:0] adder_1_out, bit_extender_1_out, multiplexer_1_out, Program_Counter_q;

  Register #(.width(16)) Program_Counter (
    .D(adder_1_out), .Q(Program_Counter_q), .clk(Clock), .clr(Clear));  // open: en
  assign bit_extender_1_out = {{15{1'b0}}, 1'b1};  // Bit_Extender bit_extender_1
  Adder #(.width(16)) adder_1 (.a(Program_Counter_q), .b(multiplexer_1_out), .out(adder_1_out));  // open: cin, cout
  Multiplexer #(.width(16)) multiplexer_1 (
    .in0(bit_extender_1_out), .in1(Immediate), .out(multiplexer_1_out), .sel(and_1_out));  // open: en
  Comparator #(.width(16), .mode("unsigned")) comparator_1 (
    .a(ALU_Output), .b(16'h1), .eq(comparator_1_eq));  // open: gt, lt
  and and_1 (and_1_out, comparator_1_eq, Is_Branch);
  ROM #(.addrWidth(16), .dataWidth(16)) rom_1 (.addr(Program_Counter_q), .data(out_8));  // open: sel

  // Notes on the sheet:
  //   contents of rom_1 (hex, n*v repeats v):
  //   c000 c101 c206 c306 c401 c502 c60a c701 c801 cf80 cd08 8ffd ce80 cd08 8eed cd10 4eed cd0f 8dd2 cc0f
  //   4cfc b0cd cd0f 8dd3 b0fd ade0 cc04 bdc fb05 cc08 bdc fb04 d004 5221 d002 4221 e305 cb0c 5b3b eb02
  //   d003 3440 4441 4334 e605 cb0f 5b6b eb02 d003 3880 4881 5b51 eb05 cb0e 5b5b eb0b d02d 7b63 fb1b cb04
  //   4b3b 7bb6 fb17 3770 4771 d024 7b62 fb08 cb04 4b2b 7bb6 fb04 3770 4771 d01b cb00 cc10 5cc1 4dfc b0db
  //   fcfd cb64 5bb1 fbff d01c cbff cc10 5cc1 4dfc b0db fcfd cb64 5bb1 fbff cb00 cc10 5cc1 4dfc b0db fcfd
  //   d00c 4cf5 cb0f b0c0 4557 4668 55b 66b 8b16 4cf5 b0cb d0a2 c206 c306 c401 c502 c701 e605 cb0f 5b6b
  //   eb02 d003 3880 4881 d095
endmodule

module Decode (
  input  [15:0] Fetch,
  output [3:0] Sr1,
  output [3:0] Opcode,
  output [3:0] Sr2,
  output [3:0] Dest,
  output [15:0] Immediate,
  output Load,
  output Store,
  output Branch,
  output Writes_to_reg,
  output I_Type
);

  wire comparator_4_lt, comparator_5_eq;

  Comparator #(.width(4), .mode("unsigned")) comparator_1 (.a(Fetch[15:12]), .b(4'b1010), .eq(Load));  // open: gt, lt
  Comparator #(.width(4), .mode("unsigned")) comparator_2 (.a(Fetch[15:12]), .b(4'b1011), .eq(Store));  // open: gt, lt
  Comparator #(.width(4), .mode("unsigned")) comparator_3 (.a(Fetch[15:12]), .b(4'b1100), .gt(Branch));  // open: eq, lt
  Comparator #(.width(4), .mode("unsigned")) comparator_4 (
    .a(Fetch[15:12]), .b(4'b1011), .lt(comparator_4_lt));  // open: gt, eq
  Comparator #(.width(4), .mode("unsigned")) comparator_5 (
    .a(Fetch[15:12]), .b(4'b1100), .eq(comparator_5_eq));  // open: gt, lt
  Comparator #(.width(4), .mode("unsigned")) comparator_6 (.a(Fetch[15:12]), .b(4'b1011), .gt(I_Type));  // open: eq, lt
  assign Immediate = {{8{Fetch[7]}}, Fetch[7:0]};  // Bit_Extender bit_extender_1
  or or_1 (Writes_to_reg, comparator_4_lt, comparator_5_eq);

  assign Dest = Fetch[11:8];
  assign Opcode = Fetch[15:12];
  assign Sr1 = Fetch[7:4];
  assign Sr2 = Fetch[3:0];
endmodule

module Read_Register (
  input  [3:0] Write_Address,
  input  Clock,
  input  Clear,
  input  W_E,
  input  [3:0] Read_Address_1,
  input  [3:0] Read_Address_2
);

  wire and_1_out, decode_1_writes_to_reg;
  wire [3:0] decode_1_opcode;

  Decode decode_1 (
    .Opcode(decode_1_opcode), .Writes_to_reg(decode_1_writes_to_reg));  // open: Fetch, Sr1, Sr2, Dest, Immediate, Load, Store, Branch, I_Type
  Register_File register_file_1 (
    .W_E(W_E), .Clock(Clock), .Clear(Clear));  // open: Write_Data, Write_Address, Read_Address_1, Read_Address_2, Read_Data_1, Read_Data_2
  and and_1 (and_1_out, 1'b1, decode_1_writes_to_reg);
endmodule
